# Fritzing sketch binary_clock (saved by Fritzing 0.9.3b)
perfboards: 2

parts:
  IC3 = IC, DIP package, 20 pins [chip_label=Attiny2313]
  IC4 = IC, DIP package, 16 pins [chip_label=UEN2003A]
  J7 = AVR ISP 6 Pin [package=2x3]
  J8 = male pin header, 1 pin [form="♂ (male)"]
  J9 = male pin header, 6 pins [form="♂ (male)"]
  J10 = male pin header, 1 pin [form="♂ (male)"]
  J11 = male pin header, 1 pin [form="♂ (male)"]
  C3 = Electrolytic Capacitor [capacitance=10µF voltage=50V package="100 mil [THT, electrolytic]"]
  R16 = Resistor [tolerance=±5% resistance=4.7k package=THT]
  R17 = Resistor [tolerance=±5% resistance=4.7k package=THT]
  R18 = Resistor [tolerance=±5% resistance=4.7k package=THT]
  R19 = Resistor [tolerance=±5% resistance=220 package=THT]
  R20 = Resistor [tolerance=±5% resistance=220 package=THT]
  R21 = Resistor [tolerance=±5% resistance=220 package=THT]
  R22 = Resistor [tolerance=±5% resistance=220 package=THT]
  R23 = Resistor [tolerance=±5% resistance=220 package=THT]
  R24 = Resistor [tolerance=±5% resistance=220 package=THT]
  Q4 = PNP-Transistor [package="TO92 [THT]"]
  Q5 = PNP-Transistor [package="TO92 [THT]"]
  Q6 = PNP-Transistor [package="TO92 [THT]"]
  R25 = Resistor [tolerance=±5% resistance=22k package=THT]
  R26 = Resistor [tolerance=±5% resistance=1.2k package=THT]  # not connected
  R27 = Resistor [tolerance=±5% resistance=5.4k package=THT]
  R28 = Resistor [tolerance=±5% resistance=1.2k package=THT]  # not connected
  J12 = female pin header, 4 pins [form="♀ (female)"]
  C4 = Electrolytic Capacitor [capacitance=22µF voltage=50V package="200 mil [THT, electrolytic]"]  # not connected
  J13 = male pin header, 1 pin [form="♂ (male)"]
  J14 = male pin header, 1 pin [form="♂ (male)"]
  Q7 = NPN-Transistor [package="TO92 [THT]"]
  J15 = male pin header, 1 pin [form="♂ (male)"]
  IC5 = IC, DIP package, 20 pins [chip_label=Attiny2313]
  IC6 = IC, DIP package, 16 pins [chip_label=UEN2003A]
  J16 = AVR ISP 6 Pin [package=2x3]
  J17 = male pin header, 1 pin [form="♂ (male)"]
  J18 = male pin header, 6 pins [form="♂ (male)"]
  J19 = male pin header, 1 pin [form="♂ (male)"]
  J20 = male pin header, 1 pin [form="♂ (male)"]
  J21 = male pin header, 1 pin [form="♂ (male)"]
  J23 = male pin header, 1 pin [form="♂ (male)"]
  C5 = Electrolytic Capacitor [capacitance=10µF voltage=50V package="100 mil [THT, electrolytic]"]
  R29 = Resistor [tolerance=±5% resistance=4.7k package=THT]
  R30 = Resistor [tolerance=±5% resistance=4.7k package=THT]
  R31 = Resistor [tolerance=±5% resistance=4.7k package=THT]
  R32 = Resistor [tolerance=±5% resistance=220 package=THT]
  R33 = Resistor [tolerance=±5% resistance=220 package=THT]
  R34 = Resistor [tolerance=±5% resistance=220 package=THT]
  R35 = Resistor [tolerance=±5% resistance=220 package=THT]
  R36 = Resistor [tolerance=±5% resistance=220 package=THT]
  R37 = Resistor [tolerance=±5% resistance=220 package=THT]
  Q8 = PNP-Transistor [package="TO92 [THT]"]
  Q9 = PNP-Transistor [package="TO92 [THT]"]
  Q10 = PNP-Transistor [package="TO92 [THT]"]
  R38 = Resistor [tolerance=±5% resistance=22k package=THT]
  R39 = Resistor [tolerance=±5% resistance=1.2k package=THT]  # not connected
  R40 = Resistor [tolerance=±5% resistance=5.4k package=THT]
  R41 = Resistor [tolerance=±5% resistance=1.2k package=THT]  # not connected
  J24 = female pin header, 4 pins [form="♀ (female)"]
  C6 = Electrolytic Capacitor [capacitance=22µF voltage=50V package="200 mil [THT, electrolytic]"]  # not connected
  J25 = male pin header, 1 pin [form="♂ (male)"]

nets:
  N1: IC3.pin1, J7.5
  N2: IC3.pin2, J12.pin3
  N3: IC3.pin3, J14.pin1
  N4: IC3.pin6, J13.pin1
  N5: IC3.pin7, R18.Pin_0
  N6: IC3.pin8, R17.Pin_0
  N7: IC3.pin9, R16.Pin_0
  N8: IC3.pin11, Q7.B
  N9: IC3.pin12, IC4.pin7
  N10: IC3.pin13, IC4.pin6
  N11: IC3.pin14, IC4.pin5
  N12: IC3.pin15, IC4.pin4
  N13: IC3.pin16, IC4.pin3
  N14: IC3.pin17, IC4.pin2, J7.4
  N15: IC3.pin18, J7.1
  N16: IC3.pin19, J7.3
  N17: IC3.pin20, Q4.C, Q6.C
  N18: IC4.pin8, J12.pin2
  N19: IC4.pin10, R23.Pin_0
  N20: IC4.pin11, R24.Pin_0
  N21: IC4.pin12, R19.Pin_0
  N22: IC4.pin13, R22.Pin_0
  N23: IC4.pin14, R21.Pin_0
  N24: IC4.pin15, R20.Pin_0
  N25: J7.2, R27.Pin_1
  N26: J8.pin1, Q4.E
  N27: J9.pin1, R20.Pin_1
  N28: J9.pin2, R21.Pin_1
  N29: J9.pin3, R22.Pin_1
  N30: J9.pin4, R19.Pin_1
  N31: J9.pin5, R24.Pin_1
  N32: J9.pin6, R23.Pin_1
  N33: J10.pin1, Q6.E
  N34: J11.pin1, Q5.E
  N35: C3.+, R27.Pin_0
  N36: R16.Pin_1, Q6.B
  N37: R17.Pin_1, Q5.B
  N38: R18.Pin_1, Q4.B
  N39: R25.Pin_0, J12.pin4
  N40: Q7.E, J15.pin1
  N41: IC5.pin1, J16.5
  N42: IC5.pin2, J24.pin3
  N43: IC5.pin3, J21.pin1
  N44: IC5.pin6, J20.pin1
  N45: IC5.pin7, R31.Pin_0
  N46: IC5.pin8, R30.Pin_0
  N47: IC5.pin9, R29.Pin_0
  N48: IC5.pin11, IC6.pin7
  N49: IC5.pin12, IC6.pin6
  N50: IC5.pin13, IC6.pin5
  N51: IC5.pin14, IC6.pin4
  N52: IC5.pin15, IC6.pin3
  N53: IC5.pin16, IC6.pin2
  N54: IC5.pin17, IC6.pin1, J16.4
  N55: IC5.pin18, J16.1
  N56: IC5.pin19, J16.3
  N57: IC5.pin20, Q8.C, Q10.C
  N58: IC6.pin9, J16.6, J24.pin2
  N59: IC6.pin10, J25.pin1
  N60: IC6.pin11, R36.Pin_0
  N61: IC6.pin12, R37.Pin_0
  N62: IC6.pin13, R32.Pin_0
  N63: IC6.pin14, R35.Pin_0
  N64: IC6.pin15, R34.Pin_0
  N65: IC6.pin16, R33.Pin_0
  N66: J16.2, R40.Pin_1
  N67: J17.pin1, Q8.E
  N68: J18.pin1, R33.Pin_1
  N69: J18.pin2, R34.Pin_1
  N70: J18.pin3, R35.Pin_1
  N71: J18.pin4, R32.Pin_1
  N72: J18.pin5, R37.Pin_1
  N73: J18.pin6, R36.Pin_1
  N74: J19.pin1, Q10.E
  N75: J23.pin1, Q9.E
  N76: C5.+, R40.Pin_0
  N77: R29.Pin_1, Q10.B
  N78: R30.Pin_1, Q9.B
  N79: R31.Pin_1, Q8.B
  N80: R38.Pin_0, J24.pin4

notes:
  <- move one down and remove useless npn
