# Fritzing sketch binary_clock (saved by Fritzing 0.9.3b)
perfboards: 1

parts:
  IC5 = IC, DIP package, 20 pins [chip_label=Attiny2313]
  IC6 = IC, DIP package, 16 pins [chip_label=UEN2003A]
  J16 = AVR ISP 6 Pin [package=2x3]
  led_row_1 = male pin header, 1 pin [form="♂ (male)"]
  leds_- = male pin header, 6 pins [form="♂ (male)"]
  led_row_3 = male pin header, 1 pin [form="♂ (male)"]
  right_button = male pin header, 1 pin [form="♂ (male)"]
  left_button = male pin header, 1 pin [form="♂ (male)"]
  led_row_2 = male pin header, 1 pin [form="♂ (male)"]
  C5 = Electrolytic Capacitor [capacitance=10µF voltage=50V package="100 mil [THT, electrolytic]"]
  R29 = Resistor [tolerance=±5% resistance=4.7k package=THT]
  R30 = Resistor [tolerance=±5% resistance=4.7k package=THT]
  R31 = Resistor [tolerance=±5% resistance=4.7k package=THT]
  R32 = Resistor [tolerance=±5% resistance=220 package=THT]
  R33 = Resistor [tolerance=±5% resistance=220 package=THT]
  R34 = Resistor [tolerance=±5% resistance=220 package=THT]
  R35 = Resistor [tolerance=±5% resistance=220 package=THT]
  R36 = Resistor [tolerance=±5% resistance=220 package=THT]
  R37 = Resistor [tolerance=±5% resistance=220 package=THT]
  Q8 = PNP-Transistor [package="TO92 [THT]"]
  Q9 = PNP-Transistor [package="TO92 [THT]"]
  Q10 = PNP-Transistor [package="TO92 [THT]"]
  R38 = Resistor [tolerance=±5% resistance=22k package=THT]
  R39 = Resistor [tolerance=±5% resistance=1.2k package=THT]  # not connected
  R40 = Resistor [tolerance=±5% resistance=5.4k package=THT]
  R41 = Resistor [tolerance=±5% resistance=1.2k package=THT]  # not connected
  DCF77 = female pin header, 4 pins [form="♀ (female)"]
  C6 = Electrolytic Capacitor [capacitance=22µF voltage=50V package="200 mil [THT, electrolytic]"]  # not connected
  active_alarm_buzzer = male pin header, 1 pin [form="♂ (male)"]

nets:
  N1: IC5.pin1, J16.5
  N2: IC5.pin2, DCF77.pin3
  N3: IC5.pin3, left_button.pin1
  N4: IC5.pin6, right_button.pin1
  N5: IC5.pin7, R31.Pin_0
  N6: IC5.pin8, R30.Pin_0
  N7: IC5.pin9, R29.Pin_0
  N8: IC5.pin11, IC6.pin7
  N9: IC5.pin12, IC6.pin6
  N10: IC5.pin13, IC6.pin5
  N11: IC5.pin14, IC6.pin4
  N12: IC5.pin15, IC6.pin3
  N13: IC5.pin16, IC6.pin2
  N14: IC5.pin17, IC6.pin1, J16.4
  N15: IC5.pin18, J16.1
  N16: IC5.pin19, J16.3
  N17: IC5.pin20, Q8.C, Q10.C
  N18: IC6.pin9, J16.6, DCF77.pin2
  N19: IC6.pin10, active_alarm_buzzer.pin1
  N20: IC6.pin11, R36.Pin_0
  N21: IC6.pin12, R37.Pin_0
  N22: IC6.pin13, R32.Pin_0
  N23: IC6.pin14, R35.Pin_0
  N24: IC6.pin15, R34.Pin_0
  N25: IC6.pin16, R33.Pin_0
  N26: J16.2, R40.Pin_1
  N27: led_row_1.pin1, Q8.E
  N28: leds_-.pin1, R33.Pin_1
  N29: leds_-.pin2, R34.Pin_1
  N30: leds_-.pin3, R35.Pin_1
  N31: leds_-.pin4, R32.Pin_1
  N32: leds_-.pin5, R37.Pin_1
  N33: leds_-.pin6, R36.Pin_1
  N34: led_row_3.pin1, Q10.E
  N35: led_row_2.pin1, Q9.E
  N36: C5.+, R40.Pin_0
  N37: R30.Pin_1, Q9.B
  N38: R31.Pin_1, Q8.B
  N39: R38.Pin_0, DCF77.pin4
